# Fritzing sketch detecteurpresence (saved by Fritzing 0.9.3b)
circuit board: 8.46667cm x 5.64444cm
breadboards: 1

parts:
  Composant1 = Arduino Uno (Rev3)
  LED1 = LED - 5mm [color="Orange (605nm)" package="5 mm [THT]"]
  R1 = Resistor [tolerance=±5% resistance=220 package=THT]
  LED2 = LED - 5mm [color="Red (633nm)" package="5 mm [THT]"]
  R2 = Resistor [tolerance=±5% resistance=220 package=THT]
  hc-sr1 = hc-sr04
  R3 = Resistor [tolerance=±5% resistance=220 package=THT]
  LED3 = LED - 5mm [color="Green (565nm)" package="5 mm [THT]"]

nets:
  N1: Composant1.D8, hc-sr1.Echo
  N2: Composant1.D9_PWM, hc-sr1.Trig
  N3: Composant1.D10_PWM/SS, R3.Pin_1
  N4: Composant1.D11_PWM/MOSI, R2.Pin_1
  N5: Composant1.D12/MISO, R1.Pin_1
  GND: Composant1.GND, LED1.cathode, LED2.cathode, hc-sr1.GND, LED3.cathode
  5V: Composant1.5V, hc-sr1.VCC
  N6: LED1.anode, R2.Pin_0
  N7: R1.Pin_0, LED3.anode
  N8: LED2.anode, R3.Pin_0

// code stored in the sketch: d_tecteur de pr_sence.ino
/*
  Arduino Kit example
  Project - Ultrasonic

  Meseaure the distance by HC-SR04 Ultrasonic Ranging Module
*/

#include "Ultrasonic.h"
int okLed = 12;
int warningLed = 11;
int alertLed = 10;
Ultrasonic ultrasonic(9, 8); //(Trig,Echo)

void setup() {
  Serial.begin(9600);
  pinMode(okLed, OUTPUT);
  pinMode(warningLed, OUTPUT);
  pinMode(alertLed, OUTPUT);
}

void loop()
{
  digitalWrite(okLed, LOW);
  digitalWrite(warningLed, LOW);
  digitalWrite(alertLed, LOW);

  int distanceInCm = ultrasonic.Ranging(CM);
  int digitalStatus;
  int ledId;

  Serial.println(distanceInCm);
  if (distanceInCm < 20) {
    ledId = warningLed;
    if (distanceInCm < 10) {
      ledId = alertLed;
    }

    for (int i = 1; i < 5; i++) {
      if (i % 2 == 0) {
        digitalStatus = LOW;
      }
      else {
        digitalStatus = HIGH;
      }
      digitalWrite(ledId, digitalStatus);
      delay(200);
    }
  }

  delay(100);
}

// code stored in the sketch: dΘtecteur de prΘsence.ino
/*!
 * Arduino presence detector project
 * Autor : thlg
 * 
 * Based on Haljia Arduino starter kit
 * http://www.haljia.com/
 * Component : 
 * - Arduino Uno
 * - Ultra sonic HC-SR04
 *
 * Released under the MIT license
 * https://opensource.org/licenses/MIT
 *
 * Date: 2017-12-26
 */

#include "Ultrasonic.h"
int warningDistance = 20;
int alertDistance = 10;
int okPlotId = 12;
int warningPlotId = 11;
int alertPlotId = 10;
int sensorTrigPlotId = 9;
int sensorEchoPlotId = 8;
int greenFlashLoopCount = 1;
Ultrasonic ultrasonic(sensorTrigPlotId, sensorEchoPlotId); //(Trig,Echo)

void setup() {
  Serial.begin(9600);
  pinMode(okPlotId, OUTPUT);
  pinMode(warningPlotId, OUTPUT);
  pinMode(alertPlotId, OUTPUT);  
}

void loop()
{
  digitalWrite(okPlotId, LOW);
  digitalWrite(warningPlotId, LOW);
  digitalWrite(alertPlotId, LOW);
  
  int distanceInCm = ultrasonic.Ranging(CM);
  Serial.println(distanceInCm);
  if (distanceInCm <= warningDistance) {
    greenFlashLoopCount = 1;
    int ledId = warningPlotId;
    if (distanceInCm <= alertDistance) {
      ledId = alertPlotId;
    }

    flashLed(ledId);
  }
  else {
    if (greenFlashLoopCount % 10 == 0) {
      digitalWrite(okPlotId, HIGH);
      delay(200);
      greenFlashLoopCount = 1;
    }
    
    greenFlashLoopCount++;
  }

  delay(100);
}

void flashLed(int ledId) {
  int digitalStatus;
  for (int i = 1; i < 5; i++) {
    if (i % 2 == 0) {
      digitalStatus = LOW;
    }
    else {
      digitalStatus = HIGH;
    }
    digitalWrite(ledId, digitalStatus);
    delay(200);
  }
}

// code stored in the sketch: d?tecteur de pr?sence.ino
/*!
 * Arduino presence detector project
 * Autor : thlg
 * 
 * Based on Haljia Arduino starter kit
 * http://www.haljia.com/
 * Component : 
 * - Arduino Uno
 * - Ultra sonic HC-SR04
 *
 * Released under the MIT license
 * https://opensource.org/licenses/MIT
 *
 * Date: 2017-12-26
 */

#include "Ultrasonic.h"
int warningDistance = 20;
int alertDistance = 10;
int okPlotId = 12;
int warningPlotId = 11;
int alertPlotId = 10;
int sensorTrigPlotId = 9;
int sensorEchoPlotId = 8;
int greenFlashLoopCount = 1;
Ultrasonic ultrasonic(sensorTrigPlotId, sensorEchoPlotId); //(Trig,Echo)

void setup() {
  Serial.begin(9600);
  pinMode(okPlotId, OUTPUT);
  pinMode(warningPlotId, OUTPUT);
  pinMode(alertPlotId, OUTPUT);  
}

void loop()
{
  digitalWrite(okPlotId, LOW);
  digitalWrite(warningPlotId, LOW);
  digitalWrite(alertPlotId, LOW);
  
  int distanceInCm = ultrasonic.Ranging(CM);
  Serial.println(distanceInCm);
  if (distanceInCm <= warningDistance) {
    greenFlashLoopCount = 1;
    int ledId = warningPlotId;
    if (distanceInCm <= alertDistance) {
      ledId = alertPlotId;
    }

    flashLed(ledId);
  }
  else {
    if (greenFlashLoopCount % 10 == 0) {
      digitalWrite(okPlotId, HIGH);
      delay(200);
      greenFlashLoopCount = 1;
    }
    
    greenFlashLoopCount++;
  }

  delay(100);
}

void flashLed(int ledId) {
  int digitalStatus;
  for (int i = 1; i < 5; i++) {
    if (i % 2 == 0) {
      digitalStatus = LOW;
    }
    else {
      digitalStatus = HIGH;
    }
    digitalWrite(ledId, digitalStatus);
    delay(200);
  }
}

// code stored in the sketch: ultrasonic.cpp
/*
  Ultrasonic.cpp - Library for HC-SR04 Ultrasonic Ranging Module.library

*/

#include <Arduino.h>
#include "Ultrasonic.h"

Ultrasonic::Ultrasonic(int TP, int EP)
{
   pinMode(TP,OUTPUT);
   pinMode(EP,INPUT);
   Trig_pin=TP;
   Echo_pin=EP;
}

long Ultrasonic::Timing()
{
  digitalWrite(Trig_pin, LOW);
  delayMicroseconds(2);
  digitalWrite(Trig_pin, HIGH);
  delayMicroseconds(10);
  digitalWrite(Trig_pin, LOW);
  duration = pulseIn(Echo_pin,HIGH);
  return duration;
}

long Ultrasonic::Ranging(int sys)
{
  Timing();
  distacne_cm = duration /29 / 2 ;
  distance_inc = duration / 74 / 2;
  if (sys)
  return distacne_cm;
  else
  return distance_inc;
}

// code stored in the sketch: Ultrasonic.h
/*
  Ultrasonic.h - Library for HC-SR04 Ultrasonic Ranging Module.library

*/

#ifndef Ultrasonic_h
#define Ultrasonic_h

#include <Arduino.h>

#define CM 1
#define INC 0


class Ultrasonic
{
  public:
    Ultrasonic(int TP, int EP);
    long Timing();
    long Ranging(int sys);

    private:
    int Trig_pin;
    int Echo_pin;
    long  duration,distacne_cm,distance_inc;
    
};

#endif
